// Logisim project CPU.circ as structural Verilog: 4 circuits, main circuit ALU
module CPU (
  input  in_1
);

  wire alu_1_out_5, and_1_out, clock_1_out, controlunit_1_alusrc, controlunit_1_beq, controlunit_1_j,
       controlunit_1_mread, controlunit_1_mtor, controlunit_1_mwrite, controlunit_1_rdst,
       controlunit_1_rwrite;
  wire [1:0] controlunit_1_aluop;
  wire [3:0] multiplexer_1_out;
  wire [15:0] adder_1_out, adder_2_out, alu_1_out_4, multiplexer_2_out, multiplexer_3_out, multiplexer_4_out,
       multiplexer_5_out, ram_2_data, regbank_1_reg1out, regbank_1_reg2out, register_1_q;
  wire [31:0] ram_1_data;

  Register #(.width(16)) register_1 (
    .D(multiplexer_4_out), .Q(register_1_q), .clk(clock_1_out), .clr(in_1));  // open: en
  Clock clock_1 (.out(clock_1_out));
  Adder #(.width(16)) adder_1 (.a(16'h1), .b(register_1_q), .out(adder_1_out));  // open: cin, cout
  RAM #(.addrWidth(16), .dataWidth(32)) ram_1 (.addr(register_1_q), .data(ram_1_data));  // open: sel, clk, ld, clr
  ControlUnit controlunit_1 (
    .in_1(ram_1_data[31:28]), .RDst(controlunit_1_rdst), .beq(controlunit_1_beq),
    .ALUsrc(controlunit_1_alusrc), .Rwrite(controlunit_1_rwrite), .Mread(controlunit_1_mread),
    .Mwrite(controlunit_1_mwrite), .ALUop(controlunit_1_aluop), .MtoR(controlunit_1_mtor), .J(controlunit_1_j));
  Adder #(.width(16)) adder_2 (.a(adder_1_out), .b(ram_1_data[15:0]), .out(adder_2_out));  // open: cin, cout
  REGBank regbank_1 (
    .R_W(controlunit_1_rwrite), .DataIn(multiplexer_5_out), .Clock(clock_1_out), .NReg1(ram_1_data[27:24]),
    .Reg1Out(regbank_1_reg1out), .NReg2(ram_1_data[23:20]), .Dest(multiplexer_1_out), .CLR(in_1),
    .Reg2Out(regbank_1_reg2out));
  Multiplexer #(.width(4), .enable("false")) multiplexer_1 (
    .in0(ram_1_data[23:20]), .in1(ram_1_data[19:16]), .out(multiplexer_1_out), .sel(controlunit_1_rdst));
  ALU alu_1 (
    .in_2(multiplexer_2_out), .out_4(alu_1_out_4), .in_1(regbank_1_reg1out), .in_3(controlunit_1_aluop),
    .out_5(alu_1_out_5));
  Multiplexer #(.width(16), .enable("false")) multiplexer_2 (
    .in0(ram_1_data[15:0]), .in1(regbank_1_reg2out), .out(multiplexer_2_out), .sel(controlunit_1_alusrc));
  and and_1 (and_1_out, controlunit_1_beq, alu_1_out_5);
  Multiplexer #(.width(16), .enable("false")) multiplexer_3 (
    .in0(adder_1_out), .in1(adder_2_out), .out(multiplexer_3_out), .sel(and_1_out));
  Multiplexer #(.width(16), .enable("false")) multiplexer_4 (
    .in0(multiplexer_3_out), .in1(ram_1_data[15:0]), .out(multiplexer_4_out), .sel(controlunit_1_j));
  RAM #(.addrWidth(16), .dataWidth(16), .bus("separate")) ram_2 (
    .addr(alu_1_out_4), .din(regbank_1_reg2out), .data(ram_2_data), .str(controlunit_1_mwrite),
    .clk(clock_1_out), .ld(controlunit_1_mread));  // open: sel, clr
  Multiplexer #(.width(16), .enable("false")) multiplexer_5 (
    .in0(alu_1_out_4), .in1(ram_2_data), .out(multiplexer_5_out), .sel(controlunit_1_mtor));
endmodule

module ALU (
  input  [15:0] in_1,
  input  [15:0] in_2,
  input  [1:0] in_3,
  output [15:0] out_4,
  output out_5
);

  wire [15:0] adder_1_out, and_1_out, or_1_out, subtractor_1_out;

  Adder #(.width(16)) adder_1 (.a(in_1), .b(in_2), .out(adder_1_out));  // open: cin, cout
  Subtractor #(.width(16)) subtractor_1 (.a(in_1), .b(in_2), .out(subtractor_1_out));  // open: bin, bout
  assign and_1_out = in_1 & in_2;  // AND_Gate and_1, 16 bits wide
  assign or_1_out = in_1 | in_2;  // OR_Gate or_1, 16 bits wide
  Multiplexer #(.select(2), .width(16), .enable("false")) multiplexer_1 (
    .in0(adder_1_out), .in1(subtractor_1_out), .in2(and_1_out), .in3(or_1_out), .out(out_4), .sel(in_3));
  nor nor_1 (out_5, out_4[0], out_4[1], out_4[2], out_4[3], out_4[4], out_4[5], out_4[6], out_4[7], out_4[8], out_4[9], out_4[10], out_4[11], out_4[12], out_4[13], out_4[14], out_4[15]);
endmodule

// REG
module REGBank (
  input  R_W,
  input  [15:0] DataIn,
  input  Clock,
  input  [3:0] NReg1,
  input  [3:0] NReg2,
  input  [3:0] Dest,
  input  CLR,
  output [15:0] Reg1Out,
  output [15:0] Reg2Out
);

  wire and_1_out, and_2_out, and_3_out, and_4_out, and_5_out, and_6_out, and_7_out, and_8_out, and_9_out,
       and_10_out, and_11_out, and_12_out, and_13_out, and_14_out, and_15_out, and_16_out, and_17_out,
       demultiplexer_1_out0, demultiplexer_1_out1, demultiplexer_1_out2, demultiplexer_1_out3,
       demultiplexer_1_out4, demultiplexer_1_out5, demultiplexer_1_out6, demultiplexer_1_out7,
       demultiplexer_1_out8, demultiplexer_1_out9, demultiplexer_1_out10, demultiplexer_1_out11,
       demultiplexer_1_out12, demultiplexer_1_out13, demultiplexer_1_out14, demultiplexer_1_out15, not_1_out;
  wire [15:0] Reg0_q, Reg1_q, Reg2_q, Reg3_q, Reg4_q, Reg5_q, Reg6_q, Reg7_q, Reg8_q, Reg9_q, Reg10_q,
       Reg11_q, Reg12_q, Reg13_q, Reg14_q, Reg15_q, register_1_q;

  Register #(.width(16), .trigger("falling")) register_1 (
    .D(DataIn), .Q(register_1_q), .clk(Clock), .clr(CLR));  // open: en
  not not_1 (not_1_out, Clock);
  Demultiplexer #(.select(4), .enable("false")) demultiplexer_1 (
    .out0(demultiplexer_1_out0), .out1(demultiplexer_1_out1), .out2(demultiplexer_1_out2),
    .out3(demultiplexer_1_out3), .out4(demultiplexer_1_out4), .out5(demultiplexer_1_out5),
    .out6(demultiplexer_1_out6), .out7(demultiplexer_1_out7), .out8(demultiplexer_1_out8),
    .out9(demultiplexer_1_out9), .out10(demultiplexer_1_out10), .out11(demultiplexer_1_out11),
    .out12(demultiplexer_1_out12), .out13(demultiplexer_1_out13), .out14(demultiplexer_1_out14),
    .out15(demultiplexer_1_out15), .in(1'b1), .sel(Dest));
  and and_1 (and_1_out, R_W, not_1_out);
  and and_2 (and_2_out, demultiplexer_1_out0, and_1_out);
  and and_3 (and_3_out, demultiplexer_1_out1, and_1_out);
  and and_4 (and_4_out, demultiplexer_1_out2, and_1_out);
  and and_5 (and_5_out, demultiplexer_1_out3, and_1_out);
  and and_6 (and_6_out, demultiplexer_1_out4, and_1_out);
  and and_7 (and_7_out, demultiplexer_1_out5, and_1_out);
  and and_8 (and_8_out, demultiplexer_1_out6, and_1_out);
  and and_9 (and_9_out, demultiplexer_1_out7, and_1_out);
  and and_10 (and_10_out, demultiplexer_1_out8, and_1_out);
  and and_11 (and_11_out, demultiplexer_1_out9, and_1_out);
  and and_12 (and_12_out, demultiplexer_1_out10, and_1_out);
  and and_13 (and_13_out, demultiplexer_1_out11, and_1_out);
  and and_14 (and_14_out, demultiplexer_1_out12, and_1_out);
  and and_15 (and_15_out, demultiplexer_1_out13, and_1_out);
  and and_16 (and_16_out, demultiplexer_1_out14, and_1_out);
  and and_17 (and_17_out, demultiplexer_1_out15, and_1_out);
  Register #(.width(16), .trigger("high")) Reg0 (.D(register_1_q), .Q(Reg0_q), .clk(and_2_out), .clr(CLR));  // open: en
  Register #(.width(16), .trigger("high")) Reg1 (.D(register_1_q), .Q(Reg1_q), .clk(and_3_out), .clr(CLR));  // open: en
  Register #(.width(16), .trigger("high")) Reg2 (.D(register_1_q), .Q(Reg2_q), .clk(and_4_out), .clr(CLR));  // open: en
  Register #(.width(16), .trigger("high")) Reg3 (.D(register_1_q), .Q(Reg3_q), .clk(and_5_out), .clr(CLR));  // open: en
  Register #(.width(16), .trigger("high")) Reg4 (.D(register_1_q), .Q(Reg4_q), .clk(and_6_out), .clr(CLR));  // open: en
  Register #(.width(16), .trigger("high")) Reg5 (.D(register_1_q), .Q(Reg5_q), .clk(and_7_out), .clr(CLR));  // open: en
  Register #(.width(16), .trigger("high")) Reg6 (.D(register_1_q), .Q(Reg6_q), .clk(and_8_out), .clr(CLR));  // open: en
  Register #(.width(16), .trigger("high")) Reg7 (.D(register_1_q), .Q(Reg7_q), .clk(and_9_out), .clr(CLR));  // open: en
  Register #(.width(16), .trigger("high")) Reg8 (
    .D(register_1_q), .Q(Reg8_q), .clk(and_10_out), .clr(CLR));  // open: en
  Register #(.width(16), .trigger("high")) Reg9 (
    .D(register_1_q), .Q(Reg9_q), .clk(and_11_out), .clr(CLR));  // open: en
  Register #(.width(16), .trigger("high")) Reg10 (
    .D(register_1_q), .Q(Reg10_q), .clk(and_12_out), .clr(CLR));  // open: en
  Register #(.width(16), .trigger("high")) Reg11 (
    .D(register_1_q), .Q(Reg11_q), .clk(and_13_out), .clr(CLR));  // open: en
  Register #(.width(16), .trigger("high")) Reg12 (
    .D(register_1_q), .Q(Reg12_q), .clk(and_14_out), .clr(CLR));  // open: en
  Register #(.width(16), .trigger("high")) Reg13 (
    .D(register_1_q), .Q(Reg13_q), .clk(and_15_out), .clr(CLR));  // open: en
  Register #(.width(16), .trigger("high")) Reg14 (
    .D(register_1_q), .Q(Reg14_q), .clk(and_16_out), .clr(CLR));  // open: en
  Register #(.width(16), .trigger("high")) Reg15 (
    .D(register_1_q), .Q(Reg15_q), .clk(and_17_out), .clr(CLR));  // open: en
  Multiplexer #(.select(4), .width(16), .enable("false")) multiplexer_1 (
    .in0(Reg0_q), .in1(Reg1_q), .in2(Reg2_q), .in3(Reg3_q), .in4(Reg4_q), .in5(Reg5_q), .in6(Reg6_q),
    .in7(Reg7_q), .in8(Reg8_q), .in9(Reg9_q), .in10(Reg10_q), .in11(Reg11_q), .in12(Reg12_q), .in13(Reg13_q),
    .in14(Reg14_q), .in15(Reg15_q), .out(Reg1Out), .sel(NReg1));
  Multiplexer #(.select(4), .width(16), .enable("false")) multiplexer_2 (
    .in0(Reg0_q), .in1(Reg1_q), .in2(Reg2_q), .in3(Reg3_q), .in4(Reg4_q), .in5(Reg5_q), .in6(Reg6_q),
    .in7(Reg7_q), .in8(Reg8_q), .in9(Reg9_q), .in10(Reg10_q), .in11(Reg11_q), .in12(Reg12_q), .in13(Reg13_q),
    .in14(Reg14_q), .in15(Reg15_q), .out(Reg2Out), .sel(NReg2));
endmodule

// Control
module ControlUnit (
  input  [3:0] in_1,
  output RDst,
  output beq,
  output Rwrite,
  output J,
  output ALUsrc,
  output MtoR,
  output Mread,
  output Mwrite,
  output [1:0] ALUop
);

  wire add_out, addi_out, and_out, or_1_out, or_2_out, sub_out;
  wire [1:0] multiplexer_1_out;

  and add (add_out, ~in_1[3], ~in_1[2], ~in_1[1], ~in_1[0]);  // AND_Gate
  and sub (sub_out, ~in_1[3], ~in_1[2], ~in_1[1], in_1[0]);  // AND_Gate
  and \and  (and_out, ~in_1[3], ~in_1[2], in_1[1], ~in_1[0]);  // AND_Gate
  or or_1 (or_1_out, add_out, sub_out, and_out, or_2_out);
  and or_2 (or_2_out, ~in_1[3], ~in_1[2], in_1[1], in_1[0]);  // AND_Gate
  and addi (addi_out, ~in_1[3], in_1[2], ~in_1[1], ~in_1[0]);  // AND_Gate
  and u_beq (beq, ~in_1[3], in_1[2], ~in_1[1], in_1[0]);  // AND_Gate
  and u_j (J, ~in_1[3], in_1[2], in_1[1], ~in_1[0]);  // AND_Gate
  and lw (Mread, ~in_1[3], in_1[2], in_1[1], in_1[0]);  // AND_Gate
  and sw (Mwrite, in_1[3], ~in_1[2], ~in_1[1], ~in_1[0]);  // AND_Gate
  Multiplexer #(.width(2), .enable("false")) multiplexer_1 (
    .in0(2'b00), .in1(2'b01), .out(multiplexer_1_out), .sel(beq));
  Multiplexer #(.width(2), .enable("false")) multiplexer_2 (
    .in0(multiplexer_1_out), .in1(in_1[1:0]), .out(ALUop), .sel(or_1_out));
  or or_3 (RDst, add_out, sub_out, and_out, or_2_out);
  or or_4 (Rwrite, add_out, sub_out, and_out, or_2_out, addi_out, Mread);
  or or_5 (ALUsrc, add_out, sub_out, beq, and_out, or_2_out);

  assign MtoR = Mread;
endmodule
